# Fritzing sketch Villa_Fohrde (saved by Fritzing 1.0.6)
breadboards: 1

parts:
  Bauteil1 = Arduino Nano (Rev3.0)
  DFRobot_DFPlayer_Mini1 = DFRobot DFPlayer Mini [part_number=DFR0299]
  Audio = Momentary Switch [package=tactile_switch_smd]
  Klingel = Momentary Switch [package=tactile_switch_smd]
  12V_Input = Header 2 [package=screwterminal-3.5mm-2_lock]
  Hörer = Header 2 [package=screwterminal-3.5mm-2_lock]
  12V_Klingel = Header 2 [package=jst-2-pth-kit]
  Klingel_2 = Header 2 [package=jst-2-pth-kit]
  LED = Header 2 [package=jst-2-pth-kit]
  LD2410S = Header 3 [package=jst-3-pth]
  Hörersensor = Header 3 [package=jst-3-pth]
  R1 = Resistor [tolerance=±5% resistance=1k package="0402 [SMD]"]
  R2 = Resistor [tolerance=±5% resistance=1k power=0.25W package=THT]
  R3 = Resistor [tolerance=±5% resistance=100 power=0.25W package=THT]
  3_3V = Breadboard Power Supply Board SMD
  5V = Breadboard Power Supply Board SMD

nets:
  GND: Bauteil1.GND, DFRobot_DFPlayer_Mini1.GND-1, DFRobot_DFPlayer_Mini1.GND-2, Audio.4, Klingel.4, 12V_Input.2, 12V_Klingel.2, LED.2, LD2410S.3, Hörersensor.2, 3_3V.GND
  N1: Bauteil1.D4, R3.Pin_0
  N2: Bauteil1.D5, Hörersensor.1
  N3: Bauteil1.D7, LD2410S.2
  N4: Bauteil1.D8, R2.Pin_0
  N5: Bauteil1.D9, R1.Pin_0
  N6: Bauteil1.D10, Audio.2
  N7: Bauteil1.D11/MOSI, Klingel_2.2
  N8: Bauteil1.D12/MISO, Klingel_2.1
  VCC: Bauteil1.5V, DFRobot_DFPlayer_Mini1.VCC, Hörersensor.3, 5V.VCC
  N9: DFRobot_DFPlayer_Mini1.RX, R1.Pin_1
  N10: DFRobot_DFPlayer_Mini1.TX, R2.Pin_1
  N11: DFRobot_DFPlayer_Mini1.SPK_1, Hörer.1
  N12: DFRobot_DFPlayer_Mini1.SPK_2, Hörer.2
  VIN: 12V_Input.1, 12V_Klingel.1, 3_3V.VIN, 5V.VIN
  N13: LED.1, R3.Pin_1
  N14: LD2410S.1, 3_3V.VCC
